# Fritzing sketch LAMPADAS (saved by Fritzing 0.8.5b)

parts:
  Componente1 = Arduino Uno (Rev3)
  U1 = G3VM-61E1 [package=g3vm-61e1]
  U2 = BATTERY-2 [package=battery-aaa]
  INTERRUPTOR_THREE_WAY = SWITCH_SPDT [package=kps-1290]
  LAMPADA = LEDs [package=led10mm]

nets:
  N1: Componente1.D8, U1.P$5
  N2: Componente1.GND, U1.P$4
  N3: Componente1.5V, U1.P$6
  N4: U1.P$1, INTERRUPTOR_THREE_WAY.S
  N5: U1.P$2, LAMPADA.C
  N6: U1.P$3, INTERRUPTOR_THREE_WAY.O
  N7: U2.-1, INTERRUPTOR_THREE_WAY.P, LAMPADA.A

notes:
  GND : PRETO
  VCC: VERMELHO
  SAIDA DIGITAL : AZUL
  SAID NALOGICA - BRANCO
  VERMELHO: FASE
  BRANCO: NEUTRO
  FASE tomada
